// Logisim project schematic.circ as structural Verilog
module fulladder (
  input  CIN,
  input  A,
  input  B,
  output SUM,
  output COUT
);

  wire and_1_out, and_2_out, xor_1_out;

  xor xor_1 (xor_1_out, A, B);
  and and_1 (and_1_out, B, A);
  xor xor_2 (SUM, CIN, xor_1_out);
  and and_2 (and_2_out, CIN, xor_1_out);
  or or_1 (COUT, and_2_out, and_1_out);
endmodule

module FA_16 (
  input  [15:0] A,
  input  CIN,
  input  [15:0] B,
  output [15:0] SUM,
  output COUT
);

  wire fa_4_1_cout, fa_4_2_cout, fa_4_3_cout;

  FA_4 fa_4_1 (.A(A[3:0]), .B(B[3:0]), .CIN(CIN), .COUT(fa_4_1_cout), .SUM(SUM[3:0]));
  FA_4 fa_4_2 (.A(A[7:4]), .B(B[7:4]), .CIN(fa_4_1_cout), .COUT(fa_4_2_cout), .SUM(SUM[7:4]));
  FA_4 fa_4_3 (.A(A[11:8]), .B(B[11:8]), .CIN(fa_4_2_cout), .COUT(fa_4_3_cout), .SUM(SUM[11:8]));
  FA_4 fa_4_4 (.A(A[15:12]), .B(B[15:12]), .CIN(fa_4_3_cout), .COUT(COUT), .SUM(SUM[15:12]));
endmodule

module FA_4 (
  input  [3:0] A,
  input  CIN,
  input  [3:0] B,
  output [3:0] SUM,
  output COUT
);

  wire fulladder_1_cout, fulladder_2_cout, fulladder_3_cout;

  fulladder fulladder_1 (.A(A[0]), .B(B[0]), .CIN(CIN), .COUT(fulladder_1_cout), .SUM(SUM[0]));
  fulladder fulladder_2 (.A(A[1]), .B(B[1]), .CIN(fulladder_1_cout), .COUT(fulladder_2_cout), .SUM(SUM[1]));
  fulladder fulladder_3 (.A(A[2]), .B(B[2]), .CIN(fulladder_2_cout), .COUT(fulladder_3_cout), .SUM(SUM[2]));
  fulladder fulladder_4 (.A(A[3]), .B(B[3]), .CIN(fulladder_3_cout), .COUT(COUT), .SUM(SUM[3]));
endmodule

module ALU (
  input  [15:0] opA,
  input  [15:0] opB,
  input  [2:0] PREFIX,
  input  [2:0] OPCODE
);

  wire [15:0] and_1_out, fa_16_1_sum, multiplexer_1_out, multiplexer_2_out, multiplexer_3_out,
       multiplexer_4_out, not_1_out, not_2_out, not_3_out, or_1_out, shift_block_1_asl, shift_block_1_asr,
       shift_block_1_lsl, shift_block_1_lsr, xor_1_out;

  assign not_1_out = ~opB;  // NOT_Gate not_1, 16 bits wide
  Multiplexer #(.select(2), .width(16)) multiplexer_1 (
    .in0(opB), .in1(not_1_out), .in2({16{1'b1}}), .in3({16{1'b0}}), .out(multiplexer_1_out), .sel(OPCODE[1:0]));
  FA_16 fa_16_1 (.B(multiplexer_1_out), .A(opA), .CIN(OPCODE[0]), .SUM(fa_16_1_sum));  // open: COUT
  assign and_1_out = opA & opB;  // AND_Gate and_1, 16 bits wide
  assign or_1_out = opA | opB;  // OR_Gate or_1, 16 bits wide
  assign not_2_out = ~opA;  // NOT_Gate not_2, 16 bits wide
  assign xor_1_out = opA ^ opB;  // XOR_Gate xor_1, 16 bits wide
  assign not_3_out = ~xor_1_out;  // NOT_Gate not_3, 16 bits wide
  Multiplexer #(.select(2), .width(16)) multiplexer_2 (
    .in0(and_1_out), .in1(or_1_out), .in2(not_2_out), .in3(not_3_out), .out(multiplexer_2_out),
    .sel(OPCODE[1:0]));
  Shift_Block shift_block_1 (
    .SHIFTER(opA), .LSL(shift_block_1_lsl), .LSR(shift_block_1_lsr), .ASL(shift_block_1_asl),
    .ASR(shift_block_1_asr));
  Multiplexer #(.select(2), .width(16)) multiplexer_3 (
    .in0(shift_block_1_lsl), .in1(shift_block_1_lsr), .in2(shift_block_1_asl), .in3(shift_block_1_asr),
    .out(multiplexer_3_out), .sel(OPCODE[1:0]));
  Multiplexer #(.select(2), .width(16)) multiplexer_4 (
    .in0({16{1'b1}}), .in1(fa_16_1_sum), .in2(multiplexer_2_out), .in3(multiplexer_3_out),
    .out(multiplexer_4_out), .sel(PREFIX[1:0]));

  // Notes on the sheet:
  //   prefix muxes output
  //   Legal Prefixes:
  //   arith out
  //   001 - Arithmetic Ops
  //   000 - ADD AB
  //   001 - SUB AB
  //   010 - DEC A
  //   011 - INC A
  //   010 - Logic Ops
  //   000 - AND AB
  //   001 - ORR AB
  //   010 - NOT A
  //   011 - EQL AB
  //   logic out
  //   shift out
  //   011 - Shift Ops
  //   000 - LSL A
  //   001 - LSR A
  //   010 - ASL A
  //   011 - ASR A
endmodule

module Shift_Block (
  input  [15:0] SHIFTER,
  output [15:0] LSL,
  output [15:0] LSR,
  output [15:0] ASL,
  output [15:0] ASR
);


  assign ASL = {SHIFTER[14:0], SHIFTER[15]};
  assign ASR = {SHIFTER[0], SHIFTER[15:1]};
  assign LSL = {SHIFTER[14:0], 1'b0};
  assign LSR = {1'b0, SHIFTER[15:1]};

  // Notes on the sheet:
  //   LSL // LSR // ASL // ASR
endmodule

module flagdesignation (
  input  CARRYIN,
  input  CARRYOUT,
  input  [15:0] in_3,
  output [15:0] out_4
);

  xor xor_1 (out_4[2], CARRYIN, CARRYOUT);
  nor nor_1 (out_4[0], in_3[0], in_3[1], in_3[2], in_3[3], in_3[4], in_3[5], in_3[6], in_3[7], in_3[8], in_3[9], in_3[10], in_3[11], in_3[12], in_3[13], in_3[14], in_3[15]);

  assign {out_4[15:3], out_4[1]} = {{12{1'b0}}, in_3[15], in_3[0]};

  // Notes on the sheet:
  //   zero // even parity (high on odd value) // overflow // negative
endmodule
