// Logisim project tower.circ as structural Verilog
module ALU (
  input  in_1,
  input  [15:0] OPA,
  input  [15:0] OPB,
  output [15:0] SUM,
  output [15:0] FLAGS
);
endmodule

module FA_16 (
  input  [15:0] A,
  input  [15:0] B,
  input  C,
  output [15:0] S,
  output O
);

  wire fa_4_1_o, fa_4_2_o, fa_4_3_o;

  FA_4 fa_4_1 (.A(A[3:0]), .B(B[3:0]), .C(C), .S(S[3:0]), .O(fa_4_1_o));
  FA_4 fa_4_2 (.A(A[7:4]), .B(B[7:4]), .C(fa_4_1_o), .S(S[7:4]), .O(fa_4_2_o));
  FA_4 fa_4_3 (.A(A[11:8]), .B(B[11:8]), .C(fa_4_2_o), .S(S[11:8]), .O(fa_4_3_o));
  FA_4 fa_4_4 (.A(A[15:12]), .B(B[15:12]), .C(fa_4_3_o), .S(S[15:12]), .O(O));
endmodule

module FA_4 (
  input  [3:0] A,
  input  [3:0] B,
  input  C,
  output [3:0] S,
  output O
);

  wire fa_1_1_o, fa_1_2_o, fa_1_3_o;

  FA_1 fa_1_1 (.A(A[0]), .B(B[0]), .C(C), .S(S[0]), .O(fa_1_1_o));
  FA_1 fa_1_2 (.A(A[1]), .B(B[1]), .C(fa_1_1_o), .S(S[1]), .O(fa_1_2_o));
  FA_1 fa_1_3 (.A(A[2]), .B(B[2]), .C(fa_1_2_o), .S(S[2]), .O(fa_1_3_o));
  FA_1 fa_1_4 (.A(A[3]), .B(B[3]), .C(fa_1_3_o), .S(S[3]), .O(O));
endmodule

module FA_1 (
  input  A,
  input  B,
  input  C,
  output S,
  output O
);

  wire and_1_out, and_2_out, xor_1_out;

  xor xor_1 (xor_1_out, A, B);
  and and_1 (and_1_out, A, B);
  xor xor_2 (S, xor_1_out, C);
  and and_2 (and_2_out, xor_1_out, C);
  or or_1 (O, and_1_out, and_2_out);
endmodule

module SH_16 (
  input  [15:0] I,
  input  L,
  input  C,
  output [15:0] O
);

  Multiplexer #(.select(2), .width(16)) multiplexer_1 (
    .in0({1'b0, I[15:1]}), .in1({I[0], I[15:1]}), .in2({I[14:0], 1'b0}), .in3({I[14:0], I[15]}), .out(O),
    .sel({L, C}));
endmodule

module BL_16 (
  input  [15:0] A,
  input  [15:0] B,
  input  [1:0] I,
  output [15:0] O
);

  wire [15:0] and_1_out, not_1_out, or_1_out, xor_1_out;

  assign and_1_out = B & A;  // AND_Gate and_1, 16 bits wide
  assign or_1_out = B | A;  // OR_Gate or_1, 16 bits wide
  assign not_1_out = ~A;  // NOT_Gate not_1, 16 bits wide
  assign xor_1_out = B ^ A;  // XOR_Gate xor_1, 16 bits wide
  Multiplexer #(.select(2), .width(16)) multiplexer_1 (
    .in0(and_1_out), .in1(or_1_out), .in2(not_1_out), .in3(xor_1_out), .out(O), .sel(I));
endmodule
